# Fritzing sketch wetterbot (saved by Fritzing 0.9.3b)
breadboards: 1

parts:
  C_H_I_P_1 = Next Thing Co. C.H.I.P
  J1 = Piezo Speaker  # not connected
  LED1 = LED - 5mm [color="Red (633nm)" package="5 mm [THT]"]  # not connected
  R1 = Resistor [tolerance=±5% resistance=220 package=THT]
  S1 = Pushbutton [package=THT]

nets:
  N1: C_H_I_P_1.XIO-P6, R1.Pin_0
  N2: C_H_I_P_1.XIO-P7, S1.leg1
  N3: C_H_I_P_1.GND, S1.leg0
